# Fritzing sketch ocb (saved by Fritzing 0.9.3b)
breadboards: 7

parts:
  Componente1 = Arduino Mega 2560 (Rev3)
  ZS-042_RTC1 = ZS-042 RTC Module
  DS3 = DS18B20 1-Wire Temperature Sensor [part_number=DS18B20]
  R2 = Resistor [tolerance=±5% resistance=4.7k package=THT]
  U3 = Nextion Display [part_number=NX8048T070_011 package=Nextion_LCD]
  DS4 = DS18B20 1-Wire Temperature Sensor Probe Cable
  R3 = Resistor [tolerance=±5% resistance=4.7k package=THT]
  Power_plug1 = Power plug
  U4 = LM2596 step down module
  Componente2 = Voltage Sensor 25V
  Componente5 = Digital FM Radio Receiver
  RE1 = KY-040 Rotary encoder [package=THT]
  SPKR1 = Loudspeaker  # not connected

nets:
  N1: Componente1.A4, Componente2.S
  N2: Componente1.D21/SCL, ZS-042_RTC1.SCL, Componente5.SCLK
  N3: Componente1.D20/SDA, ZS-042_RTC1.SDA, Componente5.SDIO
  N4: Componente1.D17_PWM/RX2, U3.TX
  N5: Componente1.D16_PWM/TX2, U3.RX
  GND: Componente1.GND, U3.GND, DS4.GND, Componente2.-
  N6: Componente1.D9_PWM, R2.Pin_0, DS4.DQ
  N7: Componente1.D8_PWM, DS3.DQ, R3.Pin_0
  VCC: Componente1.3V3, ZS-042_RTC1.VCC, Componente5.3.3V, RE1.Vcc
  N8: Componente1.D2_PWM, RE1.DT
  N9: Componente1.D3_PWM, RE1.CLK
  N10: Componente1.D4_PWM, RE1.SW
  N11: Componente1.D52, Componente5.!RST
  GND_2: ZS-042_RTC1.GND, DS3.GND, Componente5.GND, RE1.GND
  VDD: DS3.VDD, R2.Pin_1, U3.+5v, DS4.VDD, R3.Pin_1
  VCC_2: Power_plug1.VCC, U4.IN+, Componente2.VCC, Componente2.+
  GND_3: Power_plug1.GND, U4.IN-, U4.OUT-, Componente2.GND

custom parts:
  Nextion Display: Nextion NX8048T070_011 Display TFT Display
  LM2596 step down module: LM2596 DC-DC step down power supply module 3 A.
  Digital FM Radio Receiver: Description: This is a breakout board for the Silicon Laboratories Si4703 FM tuner chip. Beyond being a simple FM radio, the Si4703 is also capable of detecting and processing both Radio Data Service (RDS) and Radio Broadcast Data Service (RBDS) information. The Si4703 even does a very good job of filtering and carrier detection. It also enables data such as the station ID and song name to be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
  KY-040 Rotary encoder: KY-040 Rotary Encoder with switch on breakout borad from AZ Delivery
